# Fritzing sketch connected-kettle (saved by Fritzing 0.9.4)
breadboards: 1

parts:
  M1 = Dagu DGServo 9g (Top view) [part_number=RS001B]
  LCD1 = LCD screen
  U1 = ESP32-30Pin [part_number=ESP32-30Pin]
  R3 = Temperature Sensor (Thermistor) [thermistor_type=NTC package=THT]
  R4 = Resistor [tolerance=±5% resistance=100k package=THT]
  Load_Cell1 = Load Cell - Red/white/black/green
  Part1 = HX711 Weighing Sensor Module

nets:
  GND: M1.gnd, LCD1.VSS, LCD1.R/W, LCD1.LED-, U1.GND, R3.pin_0, Part1.GND
  VCC: M1.vcc, LCD1.VDD, U1.VIN, Part1.VCC
  N1: M1.pulse, U1.D32
  N2: LCD1.V0, U1.D27
  N3: LCD1.RS, U1.D26
  N4: LCD1.E, U1.D25
  N5: LCD1.DB4, U1.D5
  N6: LCD1.DB5, U1.D18
  N7: LCD1.DB6, U1.D19
  N8: LCD1.DB7, U1.D21
  N9: LCD1.LED+, U1.D13
  N10: U1.VP, R3.pin_1, R4.Pin_0
  N11: U1.3v3, R4.Pin_1
  N12: U1.D22, Part1.DO/RX
  N13: U1.D23, Part1.CK/TX
  N14: Load_Cell1.wire1, Part1.E+
  N15: Load_Cell1.wire2, Part1.A+
  N16: Load_Cell1.wire3, Part1.E-
  N17: Load_Cell1.wire4, Part1.A-

custom parts:
  ESP32-30Pin: Generic 30-Pin ESP32
  Load Cell - Red/white/black/green: A rectangle load cell/weighting pressure Sensor with four wires - Red, white, black, green. Normally corresponding with E+, E-, A+, A- respectively.
